# Fritzing sketch PID Car Structure (saved by Fritzing 0.9.3b)
circuit board: 8.46667cm x 5.64444cm

parts:
  Part3 = Arduino Nano (Rev3.0)
  U1 = Mini-360 DC-DC Buck converter [package=THT]
  Part1 = SparkFun Motor Driver TB6612FNG (v11) [part_number=ROB-14451]
  LED1 = LED - 5mm [color="Red (633nm)" package="5 mm [THT]"]
  S4 = SWITCH-MOMENTARY-2 [package=tactile_switch_tall]
  U2 = SWITCH_SPDT [package=kps-1290]
  VCC1 = Battery
  J1 = Piezo Speaker
  S5 = Pololu QTR-8 Reflectabce Sensor array [package=THT]
  M1 = DC Motor
  M2 = DC Motor
  R1 = Resistor [tolerance=±5% resistance=220 package=THT]
  Digital_Panel_Meter_Voltage_DMS-20PC_by_Murata1 = Digital Panel Meter, Voltage, DMS-20PC

nets:
  N1: Part3.GND, U1.IN-, S5.pin1, S5.pin15, R1.Pin_0
  N2: Part3.D4, Part1.BIN2
  N3: Part3.D5, Part1.BIN1
  N4: Part3.D6, Part1.PWMB
  N5: Part3.D7, Part1.AIN1
  N6: Part3.D8, Part1.AIN2
  N7: Part3.D9, Part1.PWMA
  N8: Part3.D11/MOSI, J1.pin2
  N9: Part3.D12/MISO, S4.1
  N10: Part3.VIN, U1.IN+, U2.P
  5V: Part3.5V, Part1.VCC, Part1.STBY, S5.pin2
  N11: Part3.A7, S5.pin3, S5.pin5
  N12: Part3.A6, S5.pin4, S5.pin6
  N13: Part3.A5, S5.pin7
  N14: Part3.A4, S5.pin8
  N15: Part3.A3, S5.pin9
  N16: Part3.A2, S5.pin10
  N17: Part3.A1, S5.pin11
  N18: Part3.A0, S5.pin12
  N19: Part3.D13/SCK, LED1.anode
  N20: U1.OUT+, Part1.VM
  N21: U1.OUT-, Part1.GND
  N22: Part1.B01, M2.pin_1
  N23: Part1.B02, M2.pin_2
  N24: Part1.A02, M1.pin_1
  N25: Part1.A01, M1.pin_2
  N26: S4.2, J1.pin1
  N27: U2.O, VCC1.+, Digital_Panel_Meter_Voltage_DMS-20PC_by_Murata1.12:_(-)_INPUT_LO
  N28: VCC1.-, Digital_Panel_Meter_Voltage_DMS-20PC_by_Murata1.11:_(+)_INPUT_HI

custom parts:
  Mini-360 DC-DC Buck converter: Mini-360 DC-DC Buck converter. Tiny buck step down voltage converter, input voltage 4.75 to 23V output 1 to 17V adjustable. Available from ebay and the like.
  SparkFun Motor Driver TB6612FNG (v11): The TB6612FNG Motor Driver can control up to two DC motors at a constant current of 1.2A (3.2A peak). Two input signals (IN1 and IN2) can be used to control the motor in one of four function modes: CW, CCW, short-brake and stop. The two motor outputs (A and B) can be separately controlled, and the speed of each motor is controlled via a PWM input signal with a frequency up to 100kHz. The STBY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
  Battery: Your standard 2x 18650 battery pack (7,4 Volts)
